// Logisim project RAM_16x8_asynch.circ as structural Verilog: 1 circuit, main circuit RAM_16x8
module RAM_16x8 (
  input  D0,
  input  D1,
  input  D2,
  input  D3,
  input  D4,
  input  D5,
  input  D6,
  input  D7,
  input  A0,
  input  A1,
  input  A2,
  input  A3,
  input  WE_N,
  input  CE_N,
  output O0_N,
  output O1_N,
  output O2_N,
  output O3_N,
  output O4_N,
  output O5_N,
  output O6_N,
  output O7_N
);

  wire and_1_out, and_2_out, not_1_out, not_2_out;
  wire [7:0] controlled_buffer_1_out;

  not not_1 (not_1_out, WE_N);
  not not_2 (not_2_out, CE_N);
  assign controlled_buffer_1_out = and_1_out ? {D7, D6, D5, D4, D3, D2, D1, D0} : 8'bz;  // Controlled_Buffer controlled_buffer_1
  and and_1 (and_1_out, not_1_out, not_2_out);
  RAM #(.addrWidth(4), .bus("asynch")) ram_1 (
    .addr({A3, A2, A1, A0}), .data(controlled_buffer_1_out), .sel(not_2_out), .ld(WE_N));  // open: clr
  assign {O7_N, O6_N, O5_N, O4_N, O3_N, O2_N, O1_N, O0_N} = and_2_out ? controlled_buffer_1_out : 8'bz;  // Controlled_Buffer controlled_buffer_2
  and and_2 (and_2_out, WE_N, not_2_out);
endmodule
