// Logisim project adder_subtracter.circ as structural Verilog: 1 circuit, main circuit adder_substr
module adder_substr (
  input  Eu,
  input  Su,
  input  A0,
  input  B0,
  input  A1,
  input  B1,
  input  A2,
  input  B2,
  input  A3,
  input  B3,
  input  A4,
  input  B4,
  input  A5,
  input  B5,
  input  A6,
  input  B6,
  input  A7,
  input  B7,
  output S0,
  output S1,
  output S2,
  output S3,
  output S4,
  output S5,
  output S6,
  output S7
);

  wire fa_1_carry, fa_1_sum, fa_2_carry, fa_2_sum, fa_3_carry, fa_3_sum, fa_4_carry, fa_4_sum, fa_5_carry,
       fa_5_sum, fa_6_carry, fa_6_sum, fa_7_carry, fa_7_sum, fa_8_sum, xor_1_out, xor_2_out, xor_3_out,
       xor_4_out, xor_5_out, xor_6_out, xor_7_out, xor_8_out;

  xor xor_1 (xor_1_out, Su, B0);
  xor xor_2 (xor_2_out, Su, B1);
  xor xor_3 (xor_3_out, Su, B2);
  xor xor_4 (xor_4_out, Su, B3);
  xor xor_5 (xor_5_out, Su, B4);
  xor xor_6 (xor_6_out, Su, B5);
  xor xor_7 (xor_7_out, Su, B6);
  xor xor_8 (xor_8_out, Su, B7);
  FA fa_1 (.Carry(fa_1_carry), .Sum(fa_1_sum), .A(A0), .B(xor_1_out), .C(Su));
  FA fa_2 (.Carry(fa_2_carry), .Sum(fa_2_sum), .A(A1), .B(xor_2_out), .C(fa_1_carry));
  FA fa_3 (.Carry(fa_3_carry), .Sum(fa_3_sum), .A(A2), .B(xor_3_out), .C(fa_2_carry));
  FA fa_4 (.Carry(fa_4_carry), .Sum(fa_4_sum), .A(A3), .B(xor_4_out), .C(fa_3_carry));
  FA fa_5 (.Carry(fa_5_carry), .Sum(fa_5_sum), .A(A4), .B(xor_5_out), .C(fa_4_carry));
  FA fa_6 (.Carry(fa_6_carry), .Sum(fa_6_sum), .A(A5), .B(xor_6_out), .C(fa_5_carry));
  FA fa_7 (.Carry(fa_7_carry), .Sum(fa_7_sum), .A(A6), .B(xor_7_out), .C(fa_6_carry));
  FA fa_8 (.Sum(fa_8_sum), .A(A7), .B(xor_8_out), .C(fa_7_carry));  // open: Carry
  assign S0 = Eu ? fa_1_sum : 1'bz;  // Controlled_Buffer controlled_buffer_1
  assign S1 = Eu ? fa_2_sum : 1'bz;  // Controlled_Buffer controlled_buffer_2
  assign S2 = Eu ? fa_3_sum : 1'bz;  // Controlled_Buffer controlled_buffer_3
  assign S3 = Eu ? fa_4_sum : 1'bz;  // Controlled_Buffer controlled_buffer_4
  assign S4 = Eu ? fa_5_sum : 1'bz;  // Controlled_Buffer controlled_buffer_5
  assign S5 = Eu ? fa_6_sum : 1'bz;  // Controlled_Buffer controlled_buffer_6
  assign S6 = Eu ? fa_7_sum : 1'bz;  // Controlled_Buffer controlled_buffer_7
  assign S7 = Eu ? fa_8_sum : 1'bz;  // Controlled_Buffer controlled_buffer_8
endmodule
