// Logisim project strobe.circ as structural Verilog: 1 circuit, main circuit main
module main (
  input  in_1,
  output out_2,
  output out_3
);

  wire d_ff_1_qn, not_1_out;

  not not_1 (not_1_out, in_1);
  and and_1 (out_2, in_1, not_1_out);
  D_Flip_Flop d_ff_1 (.clk(out_2), .D(d_ff_1_qn), .Q(out_3), .Qn(d_ff_1_qn));  // open: preset, en, reset
endmodule
