// Logisim project buffer_register_4bit.circ as structural Verilog: 1 circuit, main circuit buffer_register_4bit
module buffer_register_4bit (
  input  D0,
  input  D1,
  input  D2,
  input  D3,
  input  LOAD,
  input  CLR,
  input  CLK,
  output Q0,
  output Q1,
  output Q2,
  output Q3
);

  wire and_1_out, and_2_out, and_3_out, and_4_out, and_5_out, and_6_out, and_7_out, and_8_out, not_1_out,
       or_1_out, or_2_out, or_3_out, or_4_out;

  not not_1 (not_1_out, LOAD);
  and and_1 (and_1_out, LOAD, D0);
  and and_2 (and_2_out, not_1_out, Q0);
  or or_1 (or_1_out, and_1_out, and_2_out);
  D_Flip_Flop d_ff_1 (.clk(CLK), .D(or_1_out), .Q(Q0), .reset(CLR));  // open: Qn, preset, en
  and and_3 (and_3_out, LOAD, D1);
  or or_2 (or_2_out, and_3_out, and_4_out);
  and and_4 (and_4_out, not_1_out, Q1);
  D_Flip_Flop d_ff_2 (.clk(CLK), .D(or_2_out), .Q(Q1), .reset(CLR));  // open: Qn, preset, en
  and and_5 (and_5_out, LOAD, D2);
  and and_6 (and_6_out, not_1_out, Q2);
  or or_3 (or_3_out, and_5_out, and_6_out);
  and and_7 (and_7_out, LOAD, D3);
  D_Flip_Flop d_ff_3 (.clk(CLK), .D(or_3_out), .Q(Q2), .reset(CLR));  // open: Qn, preset, en
  and and_8 (and_8_out, not_1_out, Q3);
  or or_4 (or_4_out, and_7_out, and_8_out);
  D_Flip_Flop d_ff_4 (.clk(CLK), .D(or_4_out), .Q(Q3), .reset(CLR));  // open: Qn, preset, en
endmodule
