// Logisim project instruction_decoder.circ as structural Verilog: 1 circuit, main circuit instruction_decoder
module instruction_decoder (
  input  I7,
  input  I6,
  input  I5,
  input  I4,
  output LDA,
  output ADD,
  output SUB,
  output OUT,
  output HLT_N
);

  wire nand_1_out, nand_2_out, nand_3_out, nand_4_out, not_1_out, not_2_out, not_3_out, not_4_out;

  not not_1 (not_1_out, I7);
  not not_2 (not_2_out, I6);
  not not_3 (not_3_out, I5);
  not not_4 (not_4_out, I4);
  nand nand_1 (nand_1_out, not_4_out, not_3_out, not_2_out, not_1_out);
  not not_5 (LDA, nand_1_out);
  not not_6 (ADD, nand_2_out);
  nand nand_2 (nand_2_out, I4, not_3_out, not_2_out, not_1_out);
  not not_7 (SUB, nand_3_out);
  nand nand_3 (nand_3_out, not_4_out, I5, not_2_out, not_1_out);
  not not_8 (OUT, nand_4_out);
  nand nand_4 (nand_4_out, not_4_out, I5, I6, I7);
  nand nand_5 (HLT_N, I4, I5, I6, I7);
endmodule
