// Logisim project memory_address_register.circ as structural Verilog: 1 circuit, main circuit memory_address_register
// MAR
module memory_address_register (
  input  Lm_N,
  input  CLK,
  input  D0,
  input  D1,
  input  D2,
  input  D3,
  output Q0,
  output Q1,
  output Q2,
  output Q3
);

  wire not_1_out;

  not not_1 (not_1_out, Lm_N);
  buffer_register_4bit buffer_register_4bit_1 (
    .LOAD(not_1_out), .CLK(CLK), .D0(D0), .D1(D1), .D2(D2), .D3(D3), .Q0(Q0), .Q1(Q1), .Q2(Q2), .Q3(Q3),
    .CLR(1'b0));
endmodule
