// Logisim project accumulator.circ as structural Verilog: 1 circuit, main circuit accumulator_a
module accumulator_a (
  input  Ea,
  input  La_N,
  input  CLK,
  input  D0,
  input  D1,
  input  D2,
  input  D3,
  input  D4,
  input  D5,
  input  D6,
  input  D7,
  output Q0_Z,
  output Q1_Z,
  output Q2_Z,
  output Q3_Z,
  output Q0,
  output Q1,
  output Q2,
  output Q3,
  output Q4_Z,
  output Q5_Z,
  output Q6_Z,
  output Q7_Z,
  output Q4,
  output Q5,
  output Q6,
  output Q7
);

  wire not_1_out;

  not not_1 (not_1_out, La_N);
  buffer_register_4bit REG1 (
    .LOAD(not_1_out), .CLK(CLK), .D0(D0), .D1(D1), .D2(D2), .D3(D3), .Q0(Q0), .Q1(Q1), .Q2(Q2), .Q3(Q3),
    .CLR(1'b0));
  buffer_register_4bit REG2 (
    .LOAD(not_1_out), .CLK(CLK), .D0(D4), .D1(D5), .D2(D6), .D3(D7), .Q0(Q4), .Q1(Q5), .Q2(Q6), .Q3(Q7),
    .CLR(1'b0));
  assign Q0_Z = Ea ? Q0 : 1'bz;  // Controlled_Buffer controlled_buffer_1
  assign Q1_Z = Ea ? Q1 : 1'bz;  // Controlled_Buffer controlled_buffer_2
  assign Q2_Z = Ea ? Q2 : 1'bz;  // Controlled_Buffer controlled_buffer_3
  assign Q3_Z = Ea ? Q3 : 1'bz;  // Controlled_Buffer controlled_buffer_4
  assign Q4_Z = Ea ? Q4 : 1'bz;  // Controlled_Buffer controlled_buffer_5
  assign Q5_Z = Ea ? Q5 : 1'bz;  // Controlled_Buffer controlled_buffer_6
  assign Q6_Z = Ea ? Q6 : 1'bz;  // Controlled_Buffer controlled_buffer_7
  assign Q7_Z = Ea ? Q7 : 1'bz;  // Controlled_Buffer controlled_buffer_8
endmodule
