// Logisim project clock.circ as structural Verilog: 1 circuit, main circuit clock
module clock (
  input  GEN,
  input  HLT_N,
  output CLK,
  output CLK_N
);

  and and_1 (CLK, GEN, HLT_N);
  not not_1 (CLK_N, CLK);
endmodule
