// Logisim project control_matrix.circ as structural Verilog: 1 circuit, main circuit control_matrix
module control_matrix (
  input  T6,
  input  T5,
  input  T4,
  input  T3,
  input  T2,
  input  T1,
  input  LDA,
  input  ADD,
  input  SUB,
  input  OUT,
  output Cp,
  output Ep,
  output Lm_N,
  output CE_N,
  output Li_N,
  output Ei_N,
  output La_N,
  output Ea,
  output Su,
  output Eu,
  output Lb_N,
  output Lo_N
);

  wire nand_1_out, nand_2_out, nand_3_out, nand_4_out, nand_5_out, nand_6_out, nand_7_out, nand_8_out,
       nand_9_out, nand_10_out, nand_11_out, nand_12_out, nand_13_out, nand_14_out, nand_15_out, nand_16_out,
       nand_17_out, nand_18_out, nand_19_out, nand_20_out, nand_21_out, nand_23_out, nand_25_out, not_1_out,
       not_3_out;

  not not_1 (not_1_out, T1);
  nand nand_1 (nand_1_out, LDA, T4);
  nand nand_2 (nand_2_out, ADD, T4);
  nand nand_3 (nand_3_out, not_1_out, nand_1_out, nand_2_out, nand_4_out);
  not not_2 (Lm_N, nand_3_out);
  not not_3 (not_3_out, T3);
  nand nand_4 (nand_4_out, SUB, T4);
  nand nand_5 (nand_5_out, LDA, T5);
  nand nand_6 (nand_6_out, not_3_out, nand_5_out, nand_8_out, nand_7_out);
  not not_4 (CE_N, nand_6_out);
  nand nand_7 (nand_7_out, SUB, T5);
  nand nand_8 (nand_8_out, ADD, T5);
  not not_5 (Li_N, T3);
  nand nand_9 (nand_9_out, SUB, T4);
  nand nand_10 (nand_10_out, LDA, T4);
  nand nand_11 (nand_11_out, ADD, T4);
  nand nand_12 (nand_12_out, nand_10_out, nand_11_out, nand_9_out);
  not not_6 (Ei_N, nand_12_out);
  nand nand_13 (nand_13_out, ADD, T6);
  nand nand_14 (nand_14_out, LDA, T5);
  nand nand_15 (nand_15_out, nand_14_out, nand_13_out, nand_17_out);
  not not_7 (La_N, nand_15_out);
  nand nand_16 (nand_16_out, OUT, T4);
  nand nand_17 (nand_17_out, SUB, T6);
  not not_8 (Ea, nand_16_out);
  nand nand_18 (nand_18_out, SUB, T6);
  nand nand_19 (nand_19_out, ADD, T6);
  not not_9 (Su, nand_18_out);
  nand nand_20 (nand_20_out, ADD, T5);
  nand nand_21 (nand_21_out, SUB, T6);
  nand nand_22 (Eu, nand_19_out, nand_21_out);
  nand nand_23 (nand_23_out, SUB, T5);
  nand nand_24 (Lo_N, OUT, T4);
  nand nand_25 (nand_25_out, nand_20_out, nand_23_out);
  not not_10 (Lb_N, nand_25_out);

  assign Cp = T2;
  assign Ep = T1;
endmodule
