// Logisim project full_adder.circ as structural Verilog: 1 circuit, main circuit FA
module FA (
  input  A,
  input  B,
  input  C,
  output Carry,
  output Sum
);

  wire nand_1_out, nand_2_out, nand_3_out;

  nand nand_1 (nand_1_out, B, A);
  nand nand_2 (nand_2_out, C, A);
  nand nand_3 (nand_3_out, C, B);
  xor xor_1 (Sum, C, B, A);
  nand nand_4 (Carry, nand_1_out, nand_2_out, nand_3_out);
endmodule
