// Logisim project half_adder.circ as structural Verilog: 1 circuit, main circuit HA
module HA (
  input  A,
  input  B,
  output Sum,
  output Carry
);

  xor xor_1 (Sum, A, B);
  and and_1 (Carry, A, B);

  // Notes on the sheet:
  //   SUM = A XOR B
  //   CARRY = A AND B
endmodule
