// Logisim project instruction_register.circ as structural Verilog: 1 circuit, main circuit intruction_register
module intruction_register (
  input  Ei_N,
  input  Li_N,
  input  CLR_N,
  input  CLK,
  input  D0,
  input  D1,
  input  D2,
  input  D3,
  input  D4,
  input  D5,
  input  D6,
  input  D7,
  output Q0,
  output Q1,
  output Q2,
  output Q3,
  output I4,
  output I5,
  output I6,
  output I7
);

  wire not_1_out, not_2_out, not_3_out, REG1_q0, REG1_q1, REG1_q2, REG1_q3;

  not not_1 (not_1_out, Ei_N);
  not not_2 (not_2_out, Li_N);
  not not_3 (not_3_out, CLR_N);
  buffer_register_4bit REG1 (
    .LOAD(not_2_out), .CLK(CLK), .D0(D0), .D1(D1), .D2(D2), .D3(D3), .Q0(REG1_q0), .Q1(REG1_q1),
    .Q2(REG1_q2), .Q3(REG1_q3), .CLR(not_3_out));
  buffer_register_4bit REG2 (
    .LOAD(not_2_out), .CLK(CLK), .D0(D4), .D1(D5), .D2(D6), .D3(D7), .Q0(I4), .Q1(I5), .Q2(I6), .Q3(I7),
    .CLR(not_3_out));
  assign Q0 = not_1_out ? REG1_q0 : 1'bz;  // Controlled_Buffer controlled_buffer_1
  assign Q1 = not_1_out ? REG1_q1 : 1'bz;  // Controlled_Buffer controlled_buffer_2
  assign Q2 = not_1_out ? REG1_q2 : 1'bz;  // Controlled_Buffer controlled_buffer_3
  assign Q3 = not_1_out ? REG1_q3 : 1'bz;  // Controlled_Buffer controlled_buffer_4
endmodule
