// Logisim project nibble_multiplexer.circ as structural Verilog: 1 circuit, main circuit nibble_multiplexer
module nibble_multiplexer (
  input  S,
  input  A0,
  input  A1,
  input  A2,
  input  A3,
  input  B0,
  input  B1,
  input  B2,
  input  B3,
  output Q0,
  output Q1,
  output Q2,
  output Q3
);

  wire nand_1_out, nand_2_out, nand_3_out, nand_4_out, nand_5_out, nand_6_out, nand_7_out, nand_8_out,
       not_1_out;

  not not_1 (not_1_out, S);
  nand nand_1 (nand_1_out, S, A0);
  nand nand_2 (nand_2_out, S, A1);
  nand nand_3 (nand_3_out, S, A2);
  nand nand_4 (nand_4_out, S, A3);
  nand nand_5 (nand_5_out, not_1_out, B0);
  nand nand_6 (nand_6_out, not_1_out, B1);
  nand nand_7 (nand_7_out, not_1_out, B2);
  nand nand_8 (nand_8_out, not_1_out, B3);
  nand nand_9 (Q0, nand_1_out, nand_5_out);
  nand nand_10 (Q1, nand_2_out, nand_6_out);
  nand nand_11 (Q2, nand_3_out, nand_7_out);
  nand nand_12 (Q3, nand_4_out, nand_8_out);
endmodule
