// Logisim project output_register.circ as structural Verilog: 1 circuit, main circuit output_register
module output_register (
  input  Lo_N,
  input  CLK,
  input  D0,
  input  D1,
  input  D2,
  input  D3,
  input  D4,
  input  D5,
  input  D6,
  input  D7,
  output Q0,
  output Q1,
  output Q2,
  output Q3,
  output Q4,
  output Q5,
  output Q6,
  output Q7
);

  wire not_1_out;

  not not_1 (not_1_out, Lo_N);
  buffer_register_4bit REG1 (
    .LOAD(not_1_out), .CLK(CLK), .D0(D0), .D1(D1), .D2(D2), .D3(D3), .Q0(Q0), .Q1(Q1), .Q2(Q2), .Q3(Q3),
    .CLR(1'b0));
  buffer_register_4bit REG2 (
    .LOAD(not_1_out), .CLK(CLK), .D0(D4), .D1(D5), .D2(D6), .D3(D7), .Q0(Q4), .Q1(Q5), .Q2(Q6), .Q3(Q7),
    .CLR(1'b0));
endmodule
