// Logisim project program_counter.circ as structural Verilog: 1 circuit, main circuit program_counter
module program_counter (
  input  Cp,
  input  CLK_N,
  input  CLR_N,
  input  Ep,
  output Q0,
  output Q1,
  output Q2,
  output Q3
);

  wire j_k_ff_1_q, j_k_ff_2_q, j_k_ff_3_q, j_k_ff_4_q, not_1_out;

  not not_1 (not_1_out, CLR_N);
  J_K_Flip_Flop #(.trigger("falling")) j_k_ff_1 (
    .J(Cp), .clk(CLK_N), .K(Cp), .Q(j_k_ff_1_q), .reset(not_1_out));  // open: Qn, preset, en
  assign Q0 = Ep ? j_k_ff_1_q : 1'bz;  // Controlled_Buffer controlled_buffer_1
  J_K_Flip_Flop #(.trigger("falling")) j_k_ff_2 (
    .J(Cp), .clk(j_k_ff_1_q), .K(Cp), .Q(j_k_ff_2_q), .reset(not_1_out));  // open: Qn, preset, en
  assign Q1 = Ep ? j_k_ff_2_q : 1'bz;  // Controlled_Buffer controlled_buffer_2
  J_K_Flip_Flop #(.trigger("falling")) j_k_ff_3 (
    .J(Cp), .clk(j_k_ff_2_q), .K(Cp), .Q(j_k_ff_3_q), .reset(not_1_out));  // open: Qn, preset, en
  assign Q2 = Ep ? j_k_ff_3_q : 1'bz;  // Controlled_Buffer controlled_buffer_3
  J_K_Flip_Flop #(.trigger("falling")) j_k_ff_4 (
    .J(Cp), .clk(j_k_ff_3_q), .K(Cp), .Q(j_k_ff_4_q), .reset(not_1_out));  // open: Qn, preset, en
  assign Q3 = Ep ? j_k_ff_4_q : 1'bz;  // Controlled_Buffer controlled_buffer_4
endmodule
