// Logisim project ring_counter.circ as structural Verilog: 1 circuit, main circuit ring_counter
module ring_counter (
  input  CLK,
  input  CLR_N,
  output T1,
  output T2,
  output T3,
  output T4,
  output T5,
  output T6
);

  wire JK1_2_qn, JK1_3_qn, JK1_4_qn, JK1_5_qn, JK1_6_qn, JK1_q, not_1_out;

  not not_1 (not_1_out, CLR_N);
  J_K_Flip_Flop #(.trigger("falling")) JK1 (
    .J(JK1_6_qn), .clk(CLK), .K(T6), .Q(JK1_q), .Qn(T1), .reset(not_1_out));  // open: preset, en
  J_K_Flip_Flop #(.trigger("falling")) JK1_2 (
    .J(T1), .clk(CLK), .K(JK1_q), .Q(T2), .Qn(JK1_2_qn), .reset(not_1_out));  // open: preset, en
  J_K_Flip_Flop #(.trigger("falling")) JK1_3 (
    .J(T2), .clk(CLK), .K(JK1_2_qn), .Q(T3), .Qn(JK1_3_qn), .reset(not_1_out));  // open: preset, en
  J_K_Flip_Flop #(.trigger("falling")) JK1_4 (
    .J(T3), .clk(CLK), .K(JK1_3_qn), .Q(T4), .Qn(JK1_4_qn), .reset(not_1_out));  // open: preset, en
  J_K_Flip_Flop #(.trigger("falling")) JK1_5 (
    .J(T4), .clk(CLK), .K(JK1_4_qn), .Q(T5), .Qn(JK1_5_qn), .reset(not_1_out));  // open: preset, en
  J_K_Flip_Flop #(.trigger("falling")) JK1_6 (
    .J(T5), .clk(CLK), .K(JK1_5_qn), .Q(T6), .Qn(JK1_6_qn), .reset(not_1_out));  // open: preset, en
endmodule
