// Logisim project sap-1.circ as structural Verilog: 18 circuits, main circuit sap-1
module sap_1 (
  input  [7:0] in_1,
  input  in_2
);

  wire accumulator_1_a0, accumulator_1_a1, accumulator_1_a2, accumulator_1_a3, accumulator_1_a4,
       accumulator_1_a5, accumulator_1_a6, accumulator_1_a7, accumulator_1_l0, accumulator_1_l1,
       accumulator_1_l2, accumulator_1_l3, accumulator_1_l4, accumulator_1_l5, accumulator_1_l6,
       accumulator_1_l7, adder_subtractor_1_l0, adder_subtractor_1_l1, adder_subtractor_1_l2,
       adder_subtractor_1_l3, adder_subtractor_1_l4, adder_subtractor_1_l5, adder_subtractor_1_l6,
       adder_subtractor_1_l7, CLK, CLK_N, CLR, CLR_N, controller_sequencer_1_led_add,
       controller_sequencer_1_led_ce_n, controller_sequencer_1_led_cp, controller_sequencer_1_led_ea,
       controller_sequencer_1_led_ei_n, controller_sequencer_1_led_ep, controller_sequencer_1_led_eu,
       controller_sequencer_1_led_hlt_n, controller_sequencer_1_led_la_n, controller_sequencer_1_led_lb_n,
       controller_sequencer_1_led_lda, controller_sequencer_1_led_li_n, controller_sequencer_1_led_lm_n,
       controller_sequencer_1_led_lo_n, controller_sequencer_1_led_out, controller_sequencer_1_led_su,
       controller_sequencer_1_led_sub, controller_sequencer_1_led_t1, controller_sequencer_1_led_t2,
       controller_sequencer_1_led_t3, controller_sequencer_1_led_t4, controller_sequencer_1_led_t5,
       controller_sequencer_1_led_t6, GEN_out, HLT_N, instruction_register_1_i4, instruction_register_1_i5,
       instruction_register_1_i6, instruction_register_1_i7, instruction_register_1_l0,
       instruction_register_1_l1, instruction_register_1_l2, instruction_register_1_l3,
       instruction_register_1_l4, instruction_register_1_l5, instruction_register_1_l6,
       instruction_register_1_l7, mar_1_l0, mar_1_l1, mar_1_l2, mar_1_l3, mar_1_r0, mar_1_r1, mar_1_r2,
       mar_1_r3, not_1_out, output_register_1_l0, output_register_1_l1, output_register_1_l2,
       output_register_1_l3, output_register_1_l4, output_register_1_l5, output_register_1_l6,
       output_register_1_l7, program_counter_1_l0, program_counter_1_l1, program_counter_1_l2,
       program_counter_1_l3, register_b_1_b0, register_b_1_b1, register_b_1_b2, register_b_1_b3,
       register_b_1_b4, register_b_1_b5, register_b_1_b6, register_b_1_b7, register_b_1_l0, register_b_1_l1,
       register_b_1_l2, register_b_1_l3, register_b_1_l4, register_b_1_l5, register_b_1_l6, register_b_1_l7,
       START_CLEAR_out;
  wire [7:0] output_register_1_o0, program_counter_1_w0;
  wire [11:0] controller_sequencer_1_lo_n;

  Clock GEN (.out(GEN_out));
  Button START_CLEAR (.out(START_CLEAR_out));
  not not_1 (not_1_out, START_CLEAR_out);
  LED led_1 (.in(program_counter_1_l2));
  LED led_2 (.in(program_counter_1_l3));
  LED led_3 (.in(mar_1_l2));
  LED led_4 (.in(mar_1_l3));
  LED led_5 (.in(instruction_register_1_l7));
  LED led_6 (.in(instruction_register_1_l6));
  LED led_7 (.in(instruction_register_1_l4));
  LED led_8 (.in(instruction_register_1_l5));
  LED led_9 (.in(controller_sequencer_1_led_cp));
  LED led_10 (.in(controller_sequencer_1_led_ep));
  LED led_11 (.in(controller_sequencer_1_led_lm_n));
  LED led_12 (.in(controller_sequencer_1_led_ce_n));
  LED led_13 (.in(controller_sequencer_1_led_li_n));
  LED led_14 (.in(controller_sequencer_1_led_ei_n));
  LED led_15 (.in(controller_sequencer_1_led_la_n));
  LED led_16 (.in(controller_sequencer_1_led_ea));
  LED led_17 (.in(controller_sequencer_1_led_su));
  LED led_18 (.in(controller_sequencer_1_led_eu));
  LED led_19 (.in(controller_sequencer_1_led_lb_n));
  LED led_20 (.in(controller_sequencer_1_led_lo_n));
  clock clock_1 (.HLT_N(HLT_N), .GEN(GEN_out), .CLR(CLR), .CLK(CLK), .CLK_N(CLK_N));
  nand nand_1 (CLR_N, START_CLEAR_out, CLR);
  nand nand_2 (CLR, CLR_N, not_1_out);
  // Probe on controller_sequencer_1_lo_n
  LED led_21 (.in(program_counter_1_l1));
  LED led_22 (.in(program_counter_1_l0));
  program_counter program_counter_1 (
    .Ep(controller_sequencer_1_lo_n[10]), .Cp(controller_sequencer_1_lo_n[11]), .CLK_N(CLK_N), .CLR_N(CLR_N),
    .L0(program_counter_1_l0), .W0(program_counter_1_w0[0]), .L1(program_counter_1_l1),
    .W1(program_counter_1_w0[1]), .L2(program_counter_1_l2), .W2(program_counter_1_w0[2]),
    .L3(program_counter_1_l3), .W3(program_counter_1_w0[3]));
  LED led_23 (.in(mar_1_l0));
  LED led_24 (.in(mar_1_l1));
  MAR mar_1 (
    .W0(program_counter_1_w0[0]), .W1(program_counter_1_w0[1]), .W2(program_counter_1_w0[2]),
    .W3(program_counter_1_w0[3]), .CLK(CLK), .Lm_N(controller_sequencer_1_lo_n[9]), .R0(mar_1_r0),
    .R1(mar_1_r1), .R2(mar_1_r2), .R3(mar_1_r3), .L3(mar_1_l3), .L2(mar_1_l2), .L1(mar_1_l1), .L0(mar_1_l0),
    .CLR(CLR));
  RAM16x8 ram16x8_1 (
    .O0(program_counter_1_w0[0]), .O2(program_counter_1_w0[2]), .O3(program_counter_1_w0[3]),
    .O4(program_counter_1_w0[4]), .A0(mar_1_r0), .A1(mar_1_r1), .O6(program_counter_1_w0[6]), .A2(mar_1_r2),
    .O7(program_counter_1_w0[7]), .A3(mar_1_r3), .CE_N(controller_sequencer_1_lo_n[8]),
    .O1(program_counter_1_w0[1]), .O5(program_counter_1_w0[5]));
  LED led_25 (.in(instruction_register_1_l1));
  LED led_26 (.in(instruction_register_1_l2));
  LED led_27 (.in(instruction_register_1_l3));
  LED led_28 (.in(instruction_register_1_l0));
  instruction_register instruction_register_1 (
    .W0_IN(program_counter_1_w0[0]), .W1_IN(program_counter_1_w0[1]), .W2_IN(program_counter_1_w0[2]),
    .W3_IN(program_counter_1_w0[3]), .CLK(CLK), .CLR(CLR), .W0_IN_2(program_counter_1_w0[4]),
    .W1_IN_2(program_counter_1_w0[5]), .W2_IN_2(program_counter_1_w0[6]), .W3_IN_2(program_counter_1_w0[7]),
    .Li_N(controller_sequencer_1_lo_n[7]), .Ei_N(controller_sequencer_1_lo_n[6]),
    .L0(instruction_register_1_l0), .L1(instruction_register_1_l1), .L2(instruction_register_1_l2),
    .L3(instruction_register_1_l3), .W0_OUT(program_counter_1_w0[0]), .W1_OUT(program_counter_1_w0[1]),
    .W2_OUT(program_counter_1_w0[2]), .W3_OUT(program_counter_1_w0[3]), .L4(instruction_register_1_l4),
    .L5(instruction_register_1_l5), .L6(instruction_register_1_l6), .L7(instruction_register_1_l7),
    .I4(instruction_register_1_i4), .W4_OUT(program_counter_1_w0[4]), .I5(instruction_register_1_i5),
    .W5_OUT(program_counter_1_w0[5]), .I6(instruction_register_1_i6), .W6_OUT(program_counter_1_w0[6]),
    .I7(instruction_register_1_i7), .W7_OUT(program_counter_1_w0[7]));
  LED led_29 (.in(controller_sequencer_1_led_hlt_n));
  LED led_30 (.in(controller_sequencer_1_led_lda));
  LED led_31 (.in(controller_sequencer_1_led_add));
  LED led_32 (.in(controller_sequencer_1_led_sub));
  LED led_33 (.in(controller_sequencer_1_led_out));
  LED led_34 (.in(controller_sequencer_1_led_t1));
  LED led_35 (.in(controller_sequencer_1_led_t2));
  LED led_36 (.in(controller_sequencer_1_led_t3));
  LED led_37 (.in(controller_sequencer_1_led_t4));
  LED led_38 (.in(controller_sequencer_1_led_t5));
  LED led_39 (.in(controller_sequencer_1_led_t6));
  assign program_counter_1_w0 = in_2 ? in_1 : 8'bz;  // Controlled_Buffer controlled_buffer_1
  controller_sequencer controller_sequencer_1 (
    .CLK(CLK), .CLR_N(CLR_N), .Led_T6(controller_sequencer_1_led_t6), .Led_T5(controller_sequencer_1_led_t5),
    .Led_T4(controller_sequencer_1_led_t4), .Led_T3(controller_sequencer_1_led_t3),
    .Led_T2(controller_sequencer_1_led_t2), .Led_T1(controller_sequencer_1_led_t1),
    .Led_Cp(controller_sequencer_1_led_cp), .Led_Ep(controller_sequencer_1_led_ep),
    .Led_Lm_N(controller_sequencer_1_led_lm_n), .Led_CE_N(controller_sequencer_1_led_ce_n),
    .Led_Li_N(controller_sequencer_1_led_li_n), .Led_Ei_N(controller_sequencer_1_led_ei_n),
    .Led_La_N(controller_sequencer_1_led_la_n), .Led_Ea(controller_sequencer_1_led_ea),
    .Led_Su(controller_sequencer_1_led_su), .Led_Eu(controller_sequencer_1_led_eu),
    .Led_Lb_N(controller_sequencer_1_led_lb_n), .Led_Lo_N(controller_sequencer_1_led_lo_n),
    .Cp(controller_sequencer_1_lo_n[11]), .Ep(controller_sequencer_1_lo_n[10]),
    .Lm_N(controller_sequencer_1_lo_n[9]), .CE_N(controller_sequencer_1_lo_n[8]), .HLT_N(HLT_N),
    .Li_N(controller_sequencer_1_lo_n[7]), .Ei_N(controller_sequencer_1_lo_n[6]),
    .La_N(controller_sequencer_1_lo_n[5]), .Ea(controller_sequencer_1_lo_n[4]),
    .Su(controller_sequencer_1_lo_n[3]), .Eu(controller_sequencer_1_lo_n[2]),
    .Lb_N(controller_sequencer_1_lo_n[1]), .Lo_N(controller_sequencer_1_lo_n[0]),
    .I7(instruction_register_1_i7), .I6(instruction_register_1_i6), .I5(instruction_register_1_i5),
    .I4(instruction_register_1_i4), .Led_LDA(controller_sequencer_1_led_lda),
    .Led_ADD(controller_sequencer_1_led_add), .Led_SUB(controller_sequencer_1_led_sub),
    .Led_OUT(controller_sequencer_1_led_out), .Led_HLT_N(controller_sequencer_1_led_hlt_n));
  // Probe on program_counter_1_w0
  // Probe on program_counter_1_w0
  LED led_40 (.in(accumulator_1_l7));
  LED led_41 (.in(adder_subtractor_1_l7));
  LED led_42 (.in(register_b_1_l7));
  LED led_43 (.in(output_register_1_l7));
  LED led_44 (.in(accumulator_1_l4));
  LED led_45 (.in(accumulator_1_l3));
  LED led_46 (.in(accumulator_1_l5));
  LED led_47 (.in(accumulator_1_l6));
  LED led_48 (.in(adder_subtractor_1_l5));
  LED led_49 (.in(adder_subtractor_1_l4));
  LED led_50 (.in(adder_subtractor_1_l6));
  LED led_51 (.in(adder_subtractor_1_l3));
  LED led_52 (.in(register_b_1_l3));
  LED led_53 (.in(register_b_1_l4));
  LED led_54 (.in(register_b_1_l5));
  LED led_55 (.in(register_b_1_l6));
  LED led_56 (.in(output_register_1_l5));
  LED led_57 (.in(output_register_1_l6));
  LED led_58 (.in(output_register_1_l4));
  LED led_59 (.in(output_register_1_l3));
  LED led_60 (.in(accumulator_1_l0));
  LED led_61 (.in(accumulator_1_l1));
  LED led_62 (.in(accumulator_1_l2));
  accumulator accumulator_1 (
    .W0_IN(program_counter_1_w0[0]), .W1_IN(program_counter_1_w0[1]), .W2_IN(program_counter_1_w0[2]),
    .W3_IN(program_counter_1_w0[3]), .CLK(CLK), .CLR(CLR), .W0_IN_2(program_counter_1_w0[4]),
    .W1_IN_2(program_counter_1_w0[5]), .W2_IN_2(program_counter_1_w0[6]), .W3_IN_2(program_counter_1_w0[7]),
    .La_N(controller_sequencer_1_lo_n[5]), .L0(accumulator_1_l0), .A0(accumulator_1_a0),
    .L1(accumulator_1_l1), .A1(accumulator_1_a1), .L2(accumulator_1_l2), .A2(accumulator_1_a2),
    .L3(accumulator_1_l3), .A3(accumulator_1_a3), .W0_OUT(program_counter_1_w0[0]),
    .W1_OUT(program_counter_1_w0[1]), .W2_OUT(program_counter_1_w0[2]), .W3_OUT(program_counter_1_w0[3]),
    .L4(accumulator_1_l4), .A4(accumulator_1_a4), .L5(accumulator_1_l5), .A5(accumulator_1_a5),
    .L6(accumulator_1_l6), .A6(accumulator_1_a6), .L7(accumulator_1_l7), .A7(accumulator_1_a7),
    .W4_OUT(program_counter_1_w0[4]), .W5_OUT(program_counter_1_w0[5]), .W6_OUT(program_counter_1_w0[6]),
    .W7_OUT(program_counter_1_w0[7]), .Ea(controller_sequencer_1_lo_n[4]));
  LED led_63 (.in(adder_subtractor_1_l0));
  LED led_64 (.in(adder_subtractor_1_l1));
  LED led_65 (.in(adder_subtractor_1_l2));
  adder_subtractor adder_subtractor_1 (
    .Eu(controller_sequencer_1_lo_n[2]), .A0(accumulator_1_a0), .A1(accumulator_1_a1), .A2(accumulator_1_a2),
    .A3(accumulator_1_a3), .A4(accumulator_1_a4), .A5(accumulator_1_a5), .A6(accumulator_1_a6),
    .A7(accumulator_1_a7), .Su(controller_sequencer_1_lo_n[3]), .B0(register_b_1_b0), .B1(register_b_1_b1),
    .B2(register_b_1_b2), .B3(register_b_1_b3), .B4(register_b_1_b4), .B5(register_b_1_b5),
    .B6(register_b_1_b6), .B7(register_b_1_b7), .W0(program_counter_1_w0[0]), .W1(program_counter_1_w0[1]),
    .W2(program_counter_1_w0[2]), .W3(program_counter_1_w0[3]), .W4(program_counter_1_w0[4]),
    .W5(program_counter_1_w0[5]), .W6(program_counter_1_w0[6]), .W7(program_counter_1_w0[7]),
    .L0(adder_subtractor_1_l0), .L1(adder_subtractor_1_l1), .L2(adder_subtractor_1_l2),
    .L3(adder_subtractor_1_l3), .L4(adder_subtractor_1_l4), .L5(adder_subtractor_1_l5),
    .L6(adder_subtractor_1_l6), .L7(adder_subtractor_1_l7));
  LED led_66 (.in(register_b_1_l1));
  LED led_67 (.in(register_b_1_l0));
  LED led_68 (.in(register_b_1_l2));
  register_b register_b_1 (
    .W0_IN(program_counter_1_w0[0]), .W1_IN(program_counter_1_w0[1]), .W2_IN(program_counter_1_w0[2]),
    .W3_IN(program_counter_1_w0[3]), .CLK(CLK), .CLR(CLR), .W0_IN_2(program_counter_1_w0[4]),
    .W1_IN_2(program_counter_1_w0[5]), .W2_IN_2(program_counter_1_w0[6]), .W3_IN_2(program_counter_1_w0[7]),
    .Lb_N(controller_sequencer_1_lo_n[1]), .L0(register_b_1_l0), .L1(register_b_1_l1), .L2(register_b_1_l2),
    .L3(register_b_1_l3), .B0(register_b_1_b0), .B1(register_b_1_b1), .B2(register_b_1_b2),
    .B3(register_b_1_b3), .L4(register_b_1_l4), .L5(register_b_1_l5), .L6(register_b_1_l6),
    .L7(register_b_1_l7), .B4(register_b_1_b4), .B5(register_b_1_b5), .B6(register_b_1_b6),
    .B7(register_b_1_b7));
  LED led_69 (.in(output_register_1_l2));
  LED led_70 (.in(output_register_1_l0));
  LED led_71 (.in(output_register_1_l1));
  output_register output_register_1 (
    .W0_IN(program_counter_1_w0[0]), .W1_IN(program_counter_1_w0[1]), .W2_IN(program_counter_1_w0[2]),
    .W3_IN(program_counter_1_w0[3]), .CLK(CLK), .CLR(CLR), .W0_IN_2(program_counter_1_w0[4]),
    .W1_IN_2(program_counter_1_w0[5]), .W2_IN_2(program_counter_1_w0[6]), .W3_IN_2(program_counter_1_w0[7]),
    .Lo_N(controller_sequencer_1_lo_n[0]), .L0(output_register_1_l0), .L1(output_register_1_l1),
    .L2(output_register_1_l2), .L3(output_register_1_l3), .O0(output_register_1_o0[0]),
    .O1(output_register_1_o0[1]), .O2(output_register_1_o0[2]), .O3(output_register_1_o0[3]),
    .L4(output_register_1_l4), .L5(output_register_1_l5), .L6(output_register_1_l6),
    .L7(output_register_1_l7), .O4(output_register_1_o0[4]), .O5(output_register_1_o0[5]),
    .O6(output_register_1_o0[6]), .O7(output_register_1_o0[7]));
  // Probe on output_register_1_o0
endmodule

module program_counter (
  input  Ep,
  input  Cp,
  input  CLK_N,
  input  CLR_N,
  output L0,
  output W0,
  output L1,
  output W1,
  output L2,
  output W2,
  output L3,
  output W3
);

  IC_74107 ic_74107_1 (
    .J1(Cp), .CLK1_N(CLK_N), .K1(Cp), .CLR1_N(CLR_N), .J2(Cp), .CLK2_N(L0), .K2(Cp), .CLR2_N(CLR_N), .Q1(L0),
    .Q2(L1));  // open: Q1_N, Q2_N
  IC_74107 ic_74107_2 (
    .J1(Cp), .CLK1_N(L1), .K1(Cp), .CLR1_N(CLR_N), .J2(Cp), .CLK2_N(L2), .K2(Cp), .CLR2_N(CLR_N), .Q1(L2),
    .Q2(L3));  // open: Q1_N, Q2_N
  assign W0 = Ep ? L0 : 1'bz;  // Controlled_Buffer controlled_buffer_1
  assign W1 = Ep ? L1 : 1'bz;  // Controlled_Buffer controlled_buffer_2
  assign W2 = Ep ? L2 : 1'bz;  // Controlled_Buffer controlled_buffer_3
  assign W3 = Ep ? L3 : 1'bz;  // Controlled_Buffer controlled_buffer_4
endmodule

module MAR (
  input  W0,
  input  W1,
  input  W2,
  input  W3,
  input  CLK,
  input  Lm_N,
  input  CLR,
  output L3,
  output L2,
  output L1,
  output L0,
  output R0,
  output R1,
  output R2,
  output R3
);

  IC_74173 ic_74173_1 (
    .D1(W0), .D2(W1), .D3(W2), .D4(W3), .CLK(CLK), .CE1(Lm_N), .CE2(Lm_N), .CLR(CLR), .OE1(1'b0), .OE2(1'b0),
    .Q1(L0), .Q2(L1), .Q3(L2), .Q4(L3));
  IC_74157 ic_74157_1 (
    .A1(1'b0), .B1(L0), .A2(1'b0), .B2(L1), .A3(1'b0), .B3(L2), .A4(1'b0), .B4(L3), .S0(1'b1), .OE(1'b0),
    .Y1(R0), .Y2(R1), .Y3(R2), .Y4(R3));
endmodule

module RAM16x8 (
  input  A0,
  input  A1,
  input  A2,
  input  A3,
  input  CE_N,
  output O0,
  output O1,
  output O2,
  output O3,
  output O4,
  output O5,
  output O6,
  output O7
);

  wire and_1_out, and_2_out, not_1_out, not_2_out;
  wire [7:0] controlled_buffer_1_out;

  not not_1 (not_1_out, 1'b1);
  not not_2 (not_2_out, CE_N);
  assign controlled_buffer_1_out = and_1_out ? {8{1'b0}} : 8'bz;  // Controlled_Buffer controlled_buffer_1
  and and_1 (and_1_out, not_1_out, not_2_out);
  RAM #(.addrWidth(4), .bus("asynch")) ram_1 (
    .addr({A3, A2, A1, A0}), .data(controlled_buffer_1_out), .sel(not_2_out), .ld(1'b1));  // open: clr
  assign {O7, O6, O5, O4, O3, O2, O1, O0} = and_2_out ? controlled_buffer_1_out : 8'bz;  // Controlled_Buffer controlled_buffer_2
  and and_2 (and_2_out, 1'b1, not_2_out);
endmodule

module instruction_register (
  input  W0_IN,
  input  W1_IN,
  input  W2_IN,
  input  W3_IN,
  input  CLK,
  input  CLR,
  input  W0_IN_2,
  input  W1_IN_2,
  input  W2_IN_2,
  input  W3_IN_2,
  input  Li_N,
  input  Ei_N,
  output L0,
  output L1,
  output L2,
  output L3,
  output W0_OUT,
  output W1_OUT,
  output W2_OUT,
  output W3_OUT,
  output L4,
  output L5,
  output L6,
  output L7,
  output I4,
  output W4_OUT,
  output I5,
  output W5_OUT,
  output I6,
  output W6_OUT,
  output I7,
  output W7_OUT
);

  wire not_1_out;

  not not_1 (not_1_out, Ei_N);
  IC_74173 ic_74173_1 (
    .D1(W0_IN), .D2(W1_IN), .D3(W2_IN), .D4(W3_IN), .CLK(CLK), .CE1(Li_N), .CE2(Li_N), .CLR(CLR), .OE1(1'b0),
    .OE2(1'b0), .Q1(L0), .Q2(L1), .Q3(L2), .Q4(L3));
  IC_74173 ic_74173_2 (
    .D1(W0_IN_2), .D2(W1_IN_2), .D3(W2_IN_2), .D4(W3_IN_2), .CLK(CLK), .CE1(Li_N), .CE2(Li_N), .CLR(CLR),
    .OE1(1'b0), .OE2(1'b0), .Q1(I4), .Q2(I5), .Q3(I6), .Q4(I7));
  assign W0_OUT = not_1_out ? L0 : 1'bz;  // Controlled_Buffer controlled_buffer_1
  assign W1_OUT = not_1_out ? L1 : 1'bz;  // Controlled_Buffer controlled_buffer_2
  assign W2_OUT = not_1_out ? L2 : 1'bz;  // Controlled_Buffer controlled_buffer_3
  assign W3_OUT = not_1_out ? L3 : 1'bz;  // Controlled_Buffer controlled_buffer_4
  assign W4_OUT = not_1_out ? 1'b0 : 1'bz;  // Controlled_Buffer controlled_buffer_5
  assign W5_OUT = not_1_out ? 1'b0 : 1'bz;  // Controlled_Buffer controlled_buffer_6
  assign W6_OUT = not_1_out ? 1'b0 : 1'bz;  // Controlled_Buffer controlled_buffer_7
  assign W7_OUT = not_1_out ? 1'b0 : 1'bz;  // Controlled_Buffer controlled_buffer_8

  assign L4 = I4;
  assign L5 = I5;
  assign L6 = I6;
  assign L7 = I7;
endmodule

module controller_sequencer (
  input  CLK,
  input  CLR_N,
  input  I7,
  input  I6,
  input  I5,
  input  I4,
  output Led_Cp,
  output Led_T6,
  output Led_Ep,
  output Led_T5,
  output Led_Lm_N,
  output Led_T4,
  output Led_CE_N,
  output Led_T3,
  output Led_Li_N,
  output Led_T2,
  output Led_Ei_N,
  output Led_T1,
  output Led_La_N,
  output Led_Ea,
  output Led_Su,
  output Led_Eu,
  output Led_Lb_N,
  output Led_Lo_N,
  output Cp,
  output Ep,
  output Lm_N,
  output CE_N,
  output HLT_N,
  output Li_N,
  output Ei_N,
  output La_N,
  output Led_LDA,
  output Ea,
  output Led_ADD,
  output Su,
  output Led_SUB,
  output Eu,
  output Led_OUT,
  output Lb_N,
  output Led_HLT_N,
  output Lo_N
);

  instruction_decoder instruction_decoder_1 (
    .LDA(Led_LDA), .ADD(Led_ADD), .SUB(Led_SUB), .OUT(Led_OUT), .HLT_N(HLT_N), .I7(I7), .I6(I6), .I5(I5),
    .I4(I4));
  ring_counter ring_counter_1 (
    .CLK(CLK), .CLR_N(CLR_N), .T1(Led_T1), .T2(Led_T2), .T3(Led_T3), .T4(Led_T4), .T5(Led_T5), .T6(Led_T6));
  control_matrix control_matrix_1 (
    .Cp(Cp), .Ep(Ep), .Lm_N(Led_Lm_N), .CE_N(CE_N), .Li_N(Led_Li_N), .Ei_N(Ei_N), .La_N(La_N), .Ea(Ea),
    .Su(Led_Su), .Eu(Eu), .Lb_N(Lb_N), .Lo_N(Led_Lo_N), .T6(Led_T6), .T5(Led_T5), .T4(Led_T4), .T3(Led_T3),
    .T2(Led_T2), .T1(Led_T1), .OUT(Led_OUT), .SUB(Led_SUB), .ADD(Led_ADD), .LDA(Led_LDA));

  assign Led_CE_N = CE_N;
  assign Led_Cp = Cp;
  assign Led_Ea = Ea;
  assign Led_Ei_N = Ei_N;
  assign Led_Ep = Ep;
  assign Led_Eu = Eu;
  assign Led_HLT_N = HLT_N;
  assign Led_La_N = La_N;
  assign Led_Lb_N = Lb_N;
  assign Li_N = Led_Li_N;
  assign Lm_N = Led_Lm_N;
  assign Lo_N = Led_Lo_N;
  assign Su = Led_Su;
endmodule

module accumulator (
  input  W0_IN,
  input  W1_IN,
  input  W2_IN,
  input  W3_IN,
  input  CLK,
  input  CLR,
  input  W0_IN_2,
  input  W1_IN_2,
  input  W2_IN_2,
  input  W3_IN_2,
  input  La_N,
  input  Ea,
  output L0,
  output A0,
  output L1,
  output A1,
  output L2,
  output A2,
  output L3,
  output A3,
  output W0_OUT,
  output W1_OUT,
  output W2_OUT,
  output W3_OUT,
  output L4,
  output A4,
  output L5,
  output A5,
  output L6,
  output A6,
  output L7,
  output A7,
  output W4_OUT,
  output W5_OUT,
  output W6_OUT,
  output W7_OUT
);

  IC_74173 ic_74173_1 (
    .D1(W0_IN), .D2(W1_IN), .D3(W2_IN), .D4(W3_IN), .CLK(CLK), .CE1(La_N), .CE2(La_N), .CLR(CLR), .OE1(1'b0),
    .OE2(1'b0), .Q1(A0), .Q2(A1), .Q3(A2), .Q4(A3));
  IC_74173 ic_74173_2 (
    .D1(W0_IN_2), .D2(W1_IN_2), .D3(W2_IN_2), .D4(W3_IN_2), .CLK(CLK), .CE1(La_N), .CE2(La_N), .CLR(CLR),
    .OE1(1'b0), .OE2(1'b0), .Q1(A4), .Q2(A5), .Q3(A6), .Q4(A7));
  assign W0_OUT = Ea ? A0 : 1'bz;  // Controlled_Buffer controlled_buffer_1
  assign W1_OUT = Ea ? A1 : 1'bz;  // Controlled_Buffer controlled_buffer_2
  assign W2_OUT = Ea ? A2 : 1'bz;  // Controlled_Buffer controlled_buffer_3
  assign W3_OUT = Ea ? A3 : 1'bz;  // Controlled_Buffer controlled_buffer_4
  assign W4_OUT = Ea ? A4 : 1'bz;  // Controlled_Buffer controlled_buffer_5
  assign W5_OUT = Ea ? A5 : 1'bz;  // Controlled_Buffer controlled_buffer_6
  assign W6_OUT = Ea ? A6 : 1'bz;  // Controlled_Buffer controlled_buffer_7
  assign W7_OUT = Ea ? A7 : 1'bz;  // Controlled_Buffer controlled_buffer_8

  assign L0 = A0;
  assign L1 = A1;
  assign L2 = A2;
  assign L3 = A3;
  assign L4 = A4;
  assign L5 = A5;
  assign L6 = A6;
  assign L7 = A7;
endmodule

module adder_subtractor (
  input  Eu,
  input  A0,
  input  A1,
  input  A2,
  input  A3,
  input  A4,
  input  A5,
  input  A6,
  input  A7,
  input  Su,
  input  B0,
  input  B1,
  input  B2,
  input  B3,
  input  B4,
  input  B5,
  input  B6,
  input  B7,
  output W0,
  output W1,
  output W2,
  output W3,
  output W4,
  output W5,
  output W6,
  output W7,
  output L0,
  output L1,
  output L2,
  output L3,
  output L4,
  output L5,
  output L6,
  output L7
);

  wire ic_7486_1_y1, ic_7486_1_y2, ic_7486_1_y3, ic_7486_1_y4, ic_7486_2_y1, ic_7486_2_y2, ic_7486_2_y3,
       ic_7486_2_y4, ic_74283_1_cout;

  IC_7486 ic_7486_1 (
    .A1(B0), .B1(Su), .A2(B1), .B2(Su), .A3(B2), .B3(Su), .A4(B3), .B4(Su), .Y1(ic_7486_1_y1),
    .Y2(ic_7486_1_y2), .Y3(ic_7486_1_y3), .Y4(ic_7486_1_y4));
  IC_7486 ic_7486_2 (
    .A1(B4), .B1(Su), .A2(B5), .B2(Su), .A3(B6), .B3(Su), .A4(B7), .B4(Su), .Y1(ic_7486_2_y1),
    .Y2(ic_7486_2_y2), .Y3(ic_7486_2_y3), .Y4(ic_7486_2_y4));
  IC_74283 ic_74283_1 (
    .CIN(Su), .A1(A0), .B1(ic_7486_1_y1), .A2(A1), .B2(ic_7486_1_y2), .A3(A2), .B3(ic_7486_1_y3), .A4(A3),
    .B4(ic_7486_1_y4), .Y1(L0), .Y2(L1), .Y3(L2), .Y4(L3), .COUT(ic_74283_1_cout));
  IC_74283 ic_74283_2 (
    .CIN(ic_74283_1_cout), .A1(A4), .B1(ic_7486_2_y1), .A2(A5), .B2(ic_7486_2_y2), .A3(A6),
    .B3(ic_7486_2_y3), .A4(A7), .B4(ic_7486_2_y4), .Y1(L4), .Y2(L5), .Y3(L6), .Y4(L7));  // open: COUT
  assign W0 = Eu ? L0 : 1'bz;  // Controlled_Buffer controlled_buffer_1
  assign W1 = Eu ? L1 : 1'bz;  // Controlled_Buffer controlled_buffer_2
  assign W2 = Eu ? L2 : 1'bz;  // Controlled_Buffer controlled_buffer_3
  assign W3 = Eu ? L3 : 1'bz;  // Controlled_Buffer controlled_buffer_4
  assign W4 = Eu ? L4 : 1'bz;  // Controlled_Buffer controlled_buffer_5
  assign W5 = Eu ? L5 : 1'bz;  // Controlled_Buffer controlled_buffer_6
  assign W6 = Eu ? L6 : 1'bz;  // Controlled_Buffer controlled_buffer_7
  assign W7 = Eu ? L7 : 1'bz;  // Controlled_Buffer controlled_buffer_8
endmodule

module register_b (
  input  W0_IN,
  input  W1_IN,
  input  W2_IN,
  input  W3_IN,
  input  CLK,
  input  CLR,
  input  W0_IN_2,
  input  W1_IN_2,
  input  W2_IN_2,
  input  W3_IN_2,
  input  Lb_N,
  output L0,
  output L1,
  output L2,
  output L3,
  output B0,
  output B1,
  output B2,
  output B3,
  output L4,
  output L5,
  output L6,
  output L7,
  output B4,
  output B5,
  output B6,
  output B7
);

  IC_74173 ic_74173_1 (
    .D1(W0_IN), .D2(W1_IN), .D3(W2_IN), .D4(W3_IN), .CLK(CLK), .CE1(Lb_N), .CE2(Lb_N), .CLR(CLR), .OE1(1'b0),
    .OE2(1'b0), .Q1(B0), .Q2(B1), .Q3(B2), .Q4(B3));
  IC_74173 ic_74173_2 (
    .D1(W0_IN_2), .D2(W1_IN_2), .D3(W2_IN_2), .D4(W3_IN_2), .CLK(CLK), .CE1(Lb_N), .CE2(Lb_N), .CLR(CLR),
    .OE1(1'b0), .OE2(1'b0), .Q1(B4), .Q2(B5), .Q3(B6), .Q4(B7));

  assign L0 = B0;
  assign L1 = B1;
  assign L2 = B2;
  assign L3 = B3;
  assign L4 = B4;
  assign L5 = B5;
  assign L6 = B6;
  assign L7 = B7;
endmodule

module output_register (
  input  W0_IN,
  input  W1_IN,
  input  W2_IN,
  input  W3_IN,
  input  CLK,
  input  CLR,
  input  W0_IN_2,
  input  W1_IN_2,
  input  W2_IN_2,
  input  W3_IN_2,
  input  Lo_N,
  output L0,
  output L1,
  output L2,
  output L3,
  output O0,
  output O1,
  output O2,
  output O3,
  output L4,
  output L5,
  output L6,
  output L7,
  output O4,
  output O5,
  output O6,
  output O7
);

  IC_74173 ic_74173_1 (
    .D1(W0_IN), .D2(W1_IN), .D3(W2_IN), .D4(W3_IN), .CLK(CLK), .CE1(Lo_N), .CE2(Lo_N), .CLR(CLR), .OE1(1'b0),
    .OE2(1'b0), .Q1(L0), .Q2(L1), .Q3(L2), .Q4(L3));
  IC_74173 ic_74173_2 (
    .D1(W0_IN_2), .D2(W1_IN_2), .D3(W2_IN_2), .D4(W3_IN_2), .CLK(CLK), .CE1(Lo_N), .CE2(Lo_N), .CLR(CLR),
    .OE1(1'b0), .OE2(1'b0), .Q1(L4), .Q2(L5), .Q3(L6), .Q4(L7));

  assign O0 = L0;
  assign O1 = L1;
  assign O2 = L2;
  assign O3 = L3;
  assign O4 = L4;
  assign O5 = L5;
  assign O6 = L6;
  assign O7 = L7;
endmodule

module instruction_decoder (
  input  I7,
  input  I6,
  input  I5,
  input  I4,
  output LDA,
  output ADD,
  output SUB,
  output OUT,
  output HLT_N
);

  wire ic_7404_1_y1, ic_7404_1_y2, ic_7404_1_y3, ic_7404_1_y4, ic_7420_1_y1, ic_7420_1_y2, ic_7420_2_y1,
       ic_7420_2_y2;

  IC_7404 ic_7404_1 (
    .A1(I4), .A2(I5), .A3(I6), .A4(I7), .Y1(ic_7404_1_y1), .Y2(ic_7404_1_y2), .Y3(ic_7404_1_y3),
    .Y4(ic_7404_1_y4));  // open: A5, A6, Y5, Y6
  IC_7420 ic_7420_1 (
    .A1(ic_7404_1_y4), .A2(ic_7404_1_y4), .B1(ic_7404_1_y3), .B2(ic_7404_1_y3), .C1(ic_7404_1_y2),
    .C2(ic_7404_1_y2), .D1(ic_7404_1_y1), .D2(I4), .Y1(ic_7420_1_y1), .Y2(ic_7420_1_y2));
  IC_7420 ic_7420_2 (
    .A1(ic_7404_1_y4), .A2(I7), .B1(ic_7404_1_y3), .B2(I6), .C1(I5), .C2(I5), .D1(ic_7404_1_y1),
    .D2(ic_7404_1_y1), .Y1(ic_7420_2_y1), .Y2(ic_7420_2_y2));
  IC_7420 ic_7420_3 (.A1(I7), .B1(I6), .C1(I5), .D1(I4), .Y1(HLT_N));  // open: A2, B2, C2, D2, Y2
  IC_7404 ic_7404_2 (
    .A1(ic_7420_1_y1), .A2(ic_7420_1_y2), .A3(ic_7420_2_y1), .A4(ic_7420_2_y2), .Y1(LDA), .Y2(ADD), .Y3(SUB),
    .Y4(OUT));  // open: A5, A6, Y5, Y6
endmodule

module ring_counter (
  input  CLK,
  input  CLR_N,
  output T1,
  output T2,
  output T3,
  output T4,
  output T5,
  output T6
);

  wire j_k_ff_1_q, j_k_ff_2_qn, j_k_ff_3_qn, j_k_ff_4_qn, j_k_ff_5_qn, j_k_ff_6_qn, not_1_out;

  not not_1 (not_1_out, CLR_N);
  J_K_Flip_Flop #(.trigger("falling")) j_k_ff_1 (
    .J(j_k_ff_6_qn), .clk(CLK), .K(T6), .Q(j_k_ff_1_q), .Qn(T1), .reset(not_1_out));  // open: preset, en
  J_K_Flip_Flop #(.trigger("falling")) j_k_ff_2 (
    .J(T1), .clk(CLK), .K(j_k_ff_1_q), .Q(T2), .Qn(j_k_ff_2_qn), .reset(not_1_out));  // open: preset, en
  J_K_Flip_Flop #(.trigger("falling")) j_k_ff_3 (
    .J(T2), .clk(CLK), .K(j_k_ff_2_qn), .Q(T3), .Qn(j_k_ff_3_qn), .reset(not_1_out));  // open: preset, en
  J_K_Flip_Flop #(.trigger("falling")) j_k_ff_4 (
    .J(T3), .clk(CLK), .K(j_k_ff_3_qn), .Q(T4), .Qn(j_k_ff_4_qn), .reset(not_1_out));  // open: preset, en
  J_K_Flip_Flop #(.trigger("falling")) j_k_ff_5 (
    .J(T4), .clk(CLK), .K(j_k_ff_4_qn), .Q(T5), .Qn(j_k_ff_5_qn), .reset(not_1_out));  // open: preset, en
  J_K_Flip_Flop #(.trigger("falling")) j_k_ff_6 (
    .J(T5), .clk(CLK), .K(j_k_ff_5_qn), .Q(T6), .Qn(j_k_ff_6_qn), .reset(not_1_out));  // open: preset, en
endmodule

module control_matrix (
  input  T6,
  input  T5,
  input  T4,
  input  T3,
  input  T2,
  input  T1,
  input  OUT,
  input  SUB,
  input  ADD,
  input  LDA,
  output Cp,
  output Ep,
  output Lm_N,
  output CE_N,
  output Li_N,
  output Ei_N,
  output La_N,
  output Ea,
  output Su,
  output Eu,
  output Lb_N,
  output Lo_N
);

  wire ic_7400_1_y1, ic_7400_1_y2, ic_7400_1_y3, ic_7400_1_y4, ic_7400_2_y1, ic_7400_2_y2, ic_7400_2_y3,
       ic_7400_2_y4, ic_7400_3_y1, ic_7400_3_y2, ic_7400_3_y3, ic_7400_3_y4, ic_7400_4_y1, ic_7400_4_y2,
       ic_7400_4_y3, ic_7400_4_y4, ic_7400_5_y1, ic_7400_5_y2, ic_7400_6_y2, ic_7404_1_y1, ic_7404_1_y2,
       ic_7410_1_y1, ic_7410_1_y2, ic_7420_1_y1, ic_7420_1_y2;

  IC_7404 ic_7404_1 (.A1(T1), .A2(T3), .Y1(ic_7404_1_y1), .Y2(ic_7404_1_y2));  // open: A3, A4, A5, A6, Y3, Y4, Y5, Y6
  IC_7400 ic_7400_1 (
    .A1(LDA), .B1(T4), .A2(ADD), .B2(T4), .A3(SUB), .B3(T4), .A4(LDA), .B4(T5), .Y1(ic_7400_1_y1),
    .Y2(ic_7400_1_y2), .Y3(ic_7400_1_y3), .Y4(ic_7400_1_y4));
  IC_7400 ic_7400_2 (
    .A1(ADD), .B1(T5), .A2(SUB), .B2(T5), .A3(LDA), .B3(T4), .A4(ADD), .B4(T4), .Y1(ic_7400_2_y1),
    .Y2(ic_7400_2_y2), .Y3(ic_7400_2_y3), .Y4(ic_7400_2_y4));
  IC_7400 ic_7400_3 (
    .A1(SUB), .B1(T4), .A2(LDA), .B2(T5), .A3(ADD), .B3(T6), .A4(SUB), .B4(T6), .Y1(ic_7400_3_y1),
    .Y2(ic_7400_3_y2), .Y3(ic_7400_3_y3), .Y4(ic_7400_3_y4));
  IC_7400 ic_7400_4 (
    .A1(OUT), .B1(T4), .A2(SUB), .B2(T6), .A3(ADD), .B3(T6), .A4(SUB), .B4(T6), .Y1(ic_7400_4_y1),
    .Y2(ic_7400_4_y2), .Y3(ic_7400_4_y3), .Y4(ic_7400_4_y4));
  IC_7400 ic_7400_5 (
    .A1(ADD), .B1(T5), .A2(SUB), .B2(T5), .A3(OUT), .B3(T4), .Y1(ic_7400_5_y1), .Y2(ic_7400_5_y2), .Y3(Lo_N));  // open: A4, B4, Y4
  IC_7420 ic_7420_1 (
    .A1(ic_7404_1_y1), .A2(ic_7404_1_y2), .B1(ic_7400_1_y1), .B2(ic_7400_1_y4), .C1(ic_7400_1_y2),
    .C2(ic_7400_2_y1), .D1(ic_7400_1_y3), .D2(ic_7400_2_y2), .Y1(ic_7420_1_y1), .Y2(ic_7420_1_y2));
  IC_7410 ic_7410_1 (
    .A1(ic_7400_2_y3), .A2(ic_7400_3_y2), .B1(ic_7400_2_y4), .B2(ic_7400_3_y3), .C1(ic_7400_3_y1),
    .C2(ic_7400_3_y4), .Y1(ic_7410_1_y1), .Y2(ic_7410_1_y2));  // open: A3, B3, C3, Y3
  IC_7400 ic_7400_6 (
    .A1(ic_7400_4_y3), .B1(ic_7400_4_y4), .A2(ic_7400_5_y1), .B2(ic_7400_5_y2), .Y1(Eu), .Y2(ic_7400_6_y2));  // open: A3, B3, A4, B4, Y3, Y4
  IC_7404 ic_7404_2 (
    .A1(ic_7420_1_y1), .A2(ic_7420_1_y2), .A3(T3), .A4(ic_7410_1_y1), .A5(ic_7410_1_y2), .A6(ic_7400_4_y1),
    .Y1(Lm_N), .Y2(CE_N), .Y3(Li_N), .Y4(Ei_N), .Y5(La_N), .Y6(Ea));
  IC_7404 ic_7404_3 (.A1(ic_7400_4_y2), .A2(ic_7400_6_y2), .Y1(Su), .Y2(Lb_N));  // open: A3, A4, A5, A6, Y3, Y4, Y5, Y6

  assign Cp = T2;
  assign Ep = T1;
endmodule

module clock (
  input  HLT_N,
  input  GEN,
  input  CLR,
  output CLK,
  output CLK_N
);

  J_K_Flip_Flop j_k_ff_1 (.J(HLT_N), .clk(GEN), .K(HLT_N), .Q(CLK), .Qn(CLK_N), .reset(CLR));  // open: preset, en
endmodule

module address_ROM_16x4 (
  input  I0,
  input  I1,
  input  I2,
  input  I3,
  output V0,
  output V1,
  output V2,
  output V3
);

  ROM #(.addrWidth(4), .dataWidth(4)) rom_1 (.addr({I3, I2, I1, I0}), .data({V3, V2, V1, V0}), .sel(1'b1));

  // Notes on the sheet:
  //   contents of rom_1 (hex, n*v repeats v):
  //   3 6 9 11*f c f
endmodule

module control_ROM_16x12 (
  input  A0,
  input  A1,
  input  A2,
  input  A3,
  output Cp,
  output Ep,
  output Lm_N,
  output CE_N,
  output Li_N,
  output Ei_N,
  output La_N,
  output Ea,
  output Su,
  output Eu,
  output Lb_N,
  output Lo_N
);

  ROM #(.addrWidth(4), .dataWidth(12)) rom_1 (
    .addr({A3, A2, A1, A0}), .data({Cp, Ep, Lm_N, CE_N, Li_N, Ei_N, La_N, Ea, Su, Eu, Lb_N, Lo_N}), .sel(1'b1));

  // Notes on the sheet:
  //   contents of rom_1 (hex, n*v repeats v):
  //   5e3 be3 263 1a3 2c3 3e3 1a3 2e1 3c7 1a3 2e1 3cf 3f2 3e3 3e3
endmodule

module presettable_counter (
  input  P0,
  input  P1,
  input  P2,
  input  P3,
  input  LOAD,
  input  COUNT,
  input  CLK_N,
  input  CLR,
  output Q0,
  output Q1,
  output Q2,
  output Q3
);

  wire and_2_out, controlled_buffer_1_out, controlled_buffer_2_out, controlled_buffer_3_out,
       controlled_buffer_4_out, controlled_buffer_5_out, controlled_buffer_7_out, controlled_buffer_8_out,
       controlled_buffer_11_out, not_1_out, not_2_out, not_3_out, not_4_out, not_5_out;
  wire [1:0] and_3_out, and_6_out, and_7_out, and_9_out, register_1_q, register_2_q, register_3_q,
       register_4_q;

  not not_1 (not_1_out, CLR);
  and and_1 (and_3_out[1], P0, LOAD);
  and and_2 (and_2_out, LOAD, not_1_out);
  assign controlled_buffer_1_out = and_2_out ? register_1_q[1] : 1'bz;  // Controlled_Buffer controlled_buffer_1
  assign controlled_buffer_2_out = CLR ? CLR : 1'bz;  // Controlled_Buffer controlled_buffer_2
  assign controlled_buffer_3_out = CLR ? CLR : 1'bz;  // Controlled_Buffer controlled_buffer_3
  assign controlled_buffer_4_out = CLR ? CLR : 1'bz;  // Controlled_Buffer controlled_buffer_4
  assign controlled_buffer_5_out = CLR ? CLR : 1'bz;  // Controlled_Buffer controlled_buffer_5
  not not_2 (not_2_out, P0);
  and and_3 (and_3_out[0], not_2_out, LOAD);
  Register #(.width(2), .trigger("falling")) register_1 (
    .D(and_3_out), .Q(register_1_q), .clk(CLK_N), .clr(CLR));  // open: en
  assign controlled_buffer_2_out = and_2_out ? register_1_q[0] : 1'bz;  // Controlled_Buffer controlled_buffer_6
  J_K_Flip_Flop #(.trigger("falling")) j_k_ff_1 (
    .J(COUNT), .clk(CLK_N), .K(COUNT), .Q(Q0), .preset(controlled_buffer_1_out),
    .reset(controlled_buffer_2_out));  // open: Qn, en
  and and_4 (and_6_out[1], P1, LOAD);
  Register #(.width(2), .trigger("falling")) register_2 (
    .D(and_6_out), .Q(register_2_q), .clk(CLK_N), .clr(CLR));  // open: en
  assign controlled_buffer_7_out = and_2_out ? register_2_q[1] : 1'bz;  // Controlled_Buffer controlled_buffer_7
  J_K_Flip_Flop #(.trigger("falling")) j_k_ff_2 (
    .J(COUNT), .clk(Q0), .K(COUNT), .Q(Q1), .preset(controlled_buffer_7_out), .reset(controlled_buffer_3_out));  // open: Qn, en
  not not_3 (not_3_out, P1);
  and and_5 (and_7_out[1], P2, LOAD);
  and and_6 (and_6_out[0], not_3_out, LOAD);
  assign controlled_buffer_8_out = and_2_out ? register_3_q[1] : 1'bz;  // Controlled_Buffer controlled_buffer_8
  assign controlled_buffer_3_out = and_2_out ? register_2_q[0] : 1'bz;  // Controlled_Buffer controlled_buffer_9
  not not_4 (not_4_out, P2);
  and and_7 (and_7_out[0], not_4_out, LOAD);
  Register #(.width(2), .trigger("falling")) register_3 (
    .D(and_7_out), .Q(register_3_q), .clk(CLK_N), .clr(CLR));  // open: en
  assign controlled_buffer_4_out = and_2_out ? register_3_q[0] : 1'bz;  // Controlled_Buffer controlled_buffer_10
  J_K_Flip_Flop #(.trigger("falling")) j_k_ff_3 (
    .J(COUNT), .clk(Q1), .K(COUNT), .Q(Q2), .preset(controlled_buffer_8_out), .reset(controlled_buffer_4_out));  // open: Qn, en
  and and_8 (and_9_out[1], P3, LOAD);
  Register #(.width(2), .trigger("falling")) register_4 (
    .D(and_9_out), .Q(register_4_q), .clk(CLK_N), .clr(CLR));  // open: en
  assign controlled_buffer_11_out = and_2_out ? register_4_q[1] : 1'bz;  // Controlled_Buffer controlled_buffer_11
  J_K_Flip_Flop #(.trigger("falling")) j_k_ff_4 (
    .J(COUNT), .clk(Q2), .K(COUNT), .Q(Q3), .preset(controlled_buffer_11_out), .reset(controlled_buffer_5_out));  // open: Qn, en
  not not_5 (not_5_out, P3);
  and and_9 (and_9_out[0], not_5_out, LOAD);
  assign controlled_buffer_5_out = and_2_out ? register_4_q[0] : 1'bz;  // Controlled_Buffer controlled_buffer_12
endmodule

module microprg_control (
  input  I3,
  input  I2,
  input  I1,
  input  I0,
  input  in_5,
  input  CLR,
  output out_7,
  output out_8,
  output out_9,
  output out_10,
  output out_11,
  output out_12,
  output out_13,
  output out_14,
  output out_15,
  output out_16,
  output out_17,
  output out_18
);

  wire address_rom_16x4_1_v0, address_rom_16x4_1_v1, address_rom_16x4_1_v2, address_rom_16x4_1_v3, and_1_out,
       d_ff_1_q, d_ff_2_qn, not_1_out, not_2_out, not_3_out, not_4_out, not_5_out, not_6_out, not_7_out,
       not_8_out, not_9_out, not_10_out, not_11_out, not_12_out, not_13_out, or_1_out,
       presettable_counter_1_q0, presettable_counter_1_q1, presettable_counter_1_q2,
       presettable_counter_1_q3, ring_counter_1_t1, ring_counter_1_t3;

  ring_counter ring_counter_1 (
    .CLK(in_5), .CLR_N(1'b1), .T1(ring_counter_1_t1), .T3(ring_counter_1_t3));  // open: T2, T4, T5, T6
  or or_1 (or_1_out, ring_counter_1_t1, CLR);
  D_Flip_Flop d_ff_1 (.clk(in_5), .D(ring_counter_1_t3), .Q(d_ff_1_q));  // open: Qn, preset, en, reset
  not not_1 (not_1_out, not_9_out);
  not not_2 (not_2_out, not_10_out);
  not not_3 (not_3_out, not_12_out);
  not not_4 (not_4_out, or_1_out);
  not not_5 (not_5_out, not_4_out);
  not not_6 (not_6_out, not_7_out);
  not not_7 (not_7_out, not_1_out);
  not not_8 (not_8_out, not_2_out);
  not not_9 (not_9_out, not_8_out);
  not not_10 (not_10_out, not_11_out);
  not not_11 (not_11_out, not_3_out);
  not not_12 (not_12_out, not_13_out);
  not not_13 (not_13_out, not_5_out);
  and and_1 (and_1_out, or_1_out, not_6_out);
  D_Flip_Flop d_ff_2 (.clk(and_1_out), .D(d_ff_2_qn), .Qn(d_ff_2_qn));  // open: Q, preset, en, reset
  address_ROM_16x4 address_rom_16x4_1 (
    .I0(I0), .I1(I1), .I2(I2), .I3(I3), .V0(address_rom_16x4_1_v0), .V1(address_rom_16x4_1_v1),
    .V2(address_rom_16x4_1_v2), .V3(address_rom_16x4_1_v3));
  presettable_counter presettable_counter_1 (
    .LOAD(d_ff_1_q), .COUNT(1'b1), .CLK_N(in_5), .CLR(and_1_out), .P0(address_rom_16x4_1_v0),
    .P1(address_rom_16x4_1_v1), .P2(address_rom_16x4_1_v2), .P3(address_rom_16x4_1_v3),
    .Q0(presettable_counter_1_q0), .Q1(presettable_counter_1_q1), .Q2(presettable_counter_1_q2),
    .Q3(presettable_counter_1_q3));
  control_ROM_16x12 control_rom_16x12_1 (
    .A0(presettable_counter_1_q0), .A1(presettable_counter_1_q1), .A2(presettable_counter_1_q2),
    .A3(presettable_counter_1_q3), .Cp(out_7), .Ep(out_8), .Lm_N(out_9), .CE_N(out_10), .Li_N(out_11),
    .Ei_N(out_12), .La_N(out_13), .Ea(out_14), .Su(out_15), .Eu(out_16), .Lb_N(out_17), .Lo_N(out_18));
endmodule
